// Logisim project nand2tetris.circ as structural Verilog
module HalfAdder (
  input  a,
  input  b,
  output out,
  output carry
);

  wire and_2_out, and_3_out, not_1_out, not_2_out;

  not not_1 (not_1_out, a);
  not not_2 (not_2_out, b);
  and and_1 (carry, a, b);
  and and_2 (and_2_out, not_1_out, b);
  and and_3 (and_3_out, a, not_2_out);
  or or_1 (out, and_2_out, and_3_out);
endmodule

module Inc16 (
  input  [15:0] in_1,
  output [15:0] out_2
);

  Adder #(.width(16)) adder_1 (.a(in_1), .b(16'h1), .out(out_2));  // open: cin, cout
endmodule
